# Fritzing sketch oled_temp_monitor (saved by Fritzing 0.9.2b)

parts:
  U1 = NodeMCU V1.0
  Squix1 = OLED 0.96" 128x64 I2C SSD1306
  RHT1 = Humidity and Temperature Sensor RHT03

nets:
  N1: U1.D2, Squix1.SCA
  N2: U1.D4, Squix1.SCL
  VCC: U1.3V3, Squix1.VCC, RHT1.Vcc
  N3: U1.D7, RHT1.Data-signal
  GND: U1.GND, Squix1.GND, RHT1.GND_2

custom parts:
  NodeMCU V1.0: ESP9266 based NodeMCU
